# Fritzing sketch midterm (saved by Fritzing 0.9.3b)
breadboards: 1

parts:
  J1 = Basic Force Sensing Resistor (FSR) [package=THT]
  R1 = Resistor [tolerance=±5% resistance=220 package=THT]
  R2 = Rotary Potentiometer (Small) [maximum_resistance=100kΩ package=THT]
  Part1 = Arduino Ethernet Shield (Rev3)

nets:
  N1: J1.pin_0, R2.leg1, Part1.5V
  N2: J1.pin_1, R1.Pin_0, Part1.A0
  N3: R1.Pin_1, R2.leg2, Part1.GND
  N4: R2.wiper, Part1.A1
